# Fritzing sketch esp32_radio_remote (saved by Fritzing 0.9.5d)

parts:
  MH-ET_LIVE_ESP32_DEVKIT1 = MH-ET LIVE ESP32 DEVKIT 38 pins
  Encoder_round1 = Encoder round
  OLED1 = SSD1306 0.96in 128x64 I2C Monochrome OLED Display
  S2 = Round Pushbutton
  S3 = Round Pushbutton

nets:
  3V3: MH-ET_LIVE_ESP32_DEVKIT1.3V3, Encoder_round1.pin5, OLED1.VCC
  N1: MH-ET_LIVE_ESP32_DEVKIT1.IO32, Encoder_round1.pin2
  N2: MH-ET_LIVE_ESP32_DEVKIT1.IO33, Encoder_round1.pin3
  N3: MH-ET_LIVE_ESP32_DEVKIT1.IO25, Encoder_round1.pin4
  N4: MH-ET_LIVE_ESP32_DEVKIT1.IO26, S2.leg0
  N5: MH-ET_LIVE_ESP32_DEVKIT1.IO27, S3.leg0
  N6: MH-ET_LIVE_ESP32_DEVKIT1.GND#58, Encoder_round1.pin1, S2.leg1, S3.leg1
  N7: MH-ET_LIVE_ESP32_DEVKIT1.GND#64, OLED1.GND
  N8: MH-ET_LIVE_ESP32_DEVKIT1.IO22, OLED1.SCL
  N9: MH-ET_LIVE_ESP32_DEVKIT1.IO21, OLED1.SDA

custom parts:
  MH-ET LIVE ESP32 DEVKIT 38 pins: http://mh.nodebb.com/topic/2/mh-et-live-esp32-devkit
